# Fritzing sketch Test Circuit (saved by Fritzing 0.9.3b)
breadboards: 1

parts:
  Part1 = Arduino Nano (Rev3.0)
  Q1 = Basic FET N-Channel [part_number=FQP30N06L package="TO220 [THT]"]
  R1 = Resistor [tolerance=±5% resistance=220 package=THT]
  D1 = Rectifier Diode [package="Melf DO-213 AA [SMD]"]
  M1 = DC Motor
  R2 = Resistor [tolerance=±5% resistance=10k package=THT]

nets:
  GND: Part1.GND, Q1.source, R2.Pin_1
  N1: Part1.D3, R1.Pin_1, R2.Pin_0
  5V: Part1.VIN
  N2: Q1.gate, R1.Pin_0
  N3: Q1.drain, D1.anode, M1.pin_2
  12V: D1.cathode, M1.pin_1

notes:
  12V
  5V
